# Fritzing sketch cycle_controller (saved by Fritzing 0.9.3b)

parts:
  Digispark = Digispark
  S1 = Reed switch [package=THT]
  R1 = Resistor [tolerance=±5% resistance=10k package="2512 [SMD]"]

nets:
  N1: Digispark.VCC, S1.pin_1
  N2: Digispark.GND, R1.Pin_1
  N3: Digispark.P2, S1.pin_2, R1.Pin_0

custom parts:
  Digispark: The Digispark is an Attiny85 based microcontroller development board similar to the Arduino line, only cheaper, smaller, and a bit less powerful. With a whole host of shields to extend its functionality and the ability to use the familiar Arduino IDE the Digispark is a great way to jump into electronics, or perfect for when an Arduino is too big or too much.
